// Logisim project cpu.circ as structural Verilog: 7 circuits, main circuit main
module main (
  input  reset
);

  wire ALUsrc, clk, controller_npc_sel, ExtOp, IfBeqZero, mem2reg, memread, memwrite, regdst, regwrite, zero;
  wire [1:0] ALUOp;
  wire [3:0] ALUControl_aluoperate;
  wire [4:0] multiplexer_1_out, priority_encoder_1_out;
  wire [5:0] IFU_instr;
  wire [31:0] alu_result, multiplexer_2_out, multiplexer_3_out, PCBeq, ram_1_data, reg_rdata1, reg_rdata2;
  wire [31:6] IFU_instr_2;

  Clock u_clk (.out(clk));
  IFU IFU (.IfBeqZero(IfBeqZero), .Reset(reset), .instr({IFU_instr_2, IFU_instr}), .PCBeq(PCBeq));
  // Probe on {IFU_instr_2, IFU_instr}
  // Probe on IFU_instr
  // Probe on IFU_instr_2[31:26]
  Multiplexer #(.width(5)) multiplexer_1 (
    .in0(IFU_instr_2[15:11]), .in1(IFU_instr_2[20:16]), .out(multiplexer_1_out), .sel(regdst));  // open: en
  Control controller (
    .opcode(IFU_instr), .regdst(regdst), .alusrc(ALUsrc), .mem2reg(mem2reg), .regwrite(regwrite),
    .memwrite(memwrite), .nPC_Sel(controller_npc_sel), .ExtOp(ExtOp), .ALUOp(ALUOp), .memread(memread));
  RegFile \reg  (
    .reg1(IFU_instr_2[10:6]), .wreg(multiplexer_1_out), .regwrite(regwrite), .wdata(multiplexer_3_out),
    .reg2(IFU_instr_2[15:11]), .Rdata1(reg_rdata1), .Rdata2(reg_rdata2));
  Extender extender (.in_1(IFU_instr_2[31:16]), .ExtOp(ExtOp), .out_3(PCBeq));
  Multiplexer #(.width(32)) multiplexer_2 (
    .in0(reg_rdata2), .in1(PCBeq), .out(multiplexer_2_out), .sel(ALUsrc));  // open: en
  and and_1 (IfBeqZero, zero, controller_npc_sel);
  ALU alu (.A(reg_rdata1), .B(multiplexer_2_out), .result(alu_result), .Zero(zero), .ALUOperate(ALUControl_aluoperate));
  ALUControl ALUControl (.Funct(IFU_instr_2[31:26]), .in_2(ALUOp), .ALUOperate(ALUControl_aluoperate));
  Multiplexer #(.width(32)) multiplexer_3 (
    .in0(alu_result), .in1(ram_1_data), .out(multiplexer_3_out), .sel(mem2reg), .en(clk));
  Priority_Encoder #(.select(5)) priority_encoder_1 (
    .in0(alu_result[1]), .in1(alu_result[2]), .in2(alu_result[3]), .in3(alu_result[4]), .in4(alu_result[5]),
    .in5(alu_result[6]), .in6(alu_result[7]), .in7(alu_result[8]), .in8(alu_result[9]), .in9(alu_result[10]),
    .in10(alu_result[11]), .in11(alu_result[12]), .in12(alu_result[13]), .in13(alu_result[14]),
    .in14(alu_result[15]), .in15(alu_result[16]), .in16(alu_result[17]), .in17(alu_result[18]),
    .in18(alu_result[19]), .in19(alu_result[20]), .in20(alu_result[21]), .in21(alu_result[22]),
    .in22(alu_result[23]), .in23(alu_result[24]), .in24(alu_result[25]), .in25(alu_result[26]),
    .in26(alu_result[27]), .in27(alu_result[28]), .in28(alu_result[29]), .in29(alu_result[30]),
    .in30(alu_result[31]), .out(priority_encoder_1_out));  // open: in31, gs, en_out, en_in
  RAM #(.addrWidth(5), .dataWidth(32), .bus("separate")) ram_1 (
    .addr(priority_encoder_1_out), .din(reg_rdata2), .data(ram_1_data), .str(memwrite), .clk(clk),
    .ld(memread));  // open: sel, clr

  // Notes on the sheet:
  //   opcode
  //   funct
  //   regdst
  //   ALUsrc
  //   mem2reg
  //   regwrite
  //   memwrite
  //   nPC_Sef
  //   ExtOp
  //   ALUOp
endmodule

module RegFile (
  input  [4:0] reg1,
  input  [4:0] wreg,
  input  regwrite,
  input  [31:0] wdata,
  input  [4:0] reg2,
  output [31:0] Rdata1,
  output [31:0] Rdata2
);

  wire and_1_out, and_2_out, and_3_out, and_4_out, and_5_out, and_6_out, and_7_out, and_8_out, and_9_out,
       and_10_out, and_11_out, and_12_out, and_13_out, and_14_out, and_15_out, and_16_out, and_17_out,
       and_18_out, and_19_out, and_20_out, and_21_out, and_22_out, and_23_out, and_24_out, and_25_out,
       and_26_out, and_27_out, and_28_out, and_29_out, and_30_out, and_31_out, and_32_out, clock_1_out,
       decoder_1_out0, decoder_1_out1, decoder_1_out2, decoder_1_out3, decoder_1_out4, decoder_1_out5,
       decoder_1_out6, decoder_1_out7, decoder_1_out8, decoder_1_out9, decoder_1_out10, decoder_1_out11,
       decoder_1_out12, decoder_1_out13, decoder_1_out14, decoder_1_out15, decoder_1_out16, decoder_1_out17,
       decoder_1_out18, decoder_1_out19, decoder_1_out20, decoder_1_out21, decoder_1_out22, decoder_1_out23,
       decoder_1_out24, decoder_1_out25, decoder_1_out26, decoder_1_out27, decoder_1_out28, decoder_1_out29,
       decoder_1_out30, decoder_1_out31;
  wire [31:0] reg0_q, reg1_q, reg2_q, reg3_q, reg4_q, reg5_q, reg6_q, reg7_q, reg8_q, reg9_q, reg10_q,
       reg11_q, reg12_q, reg13_q, reg14_q, reg15_q, reg16_q, reg17_q, reg18_q, reg19_q, reg20_q, reg21_q,
       reg22_q, reg23_q, reg24_q, reg25_q, reg26_q, reg27_q, reg28_q, reg29_q, reg30_q, reg31_q;

  Clock clock_1 (.out(clock_1_out));
  Decoder #(.select(5), .enable("false")) decoder_1 (
    .out0(decoder_1_out0), .out1(decoder_1_out1), .out2(decoder_1_out2), .out3(decoder_1_out3),
    .out4(decoder_1_out4), .out5(decoder_1_out5), .out6(decoder_1_out6), .out7(decoder_1_out7),
    .out8(decoder_1_out8), .out9(decoder_1_out9), .out10(decoder_1_out10), .out11(decoder_1_out11),
    .out12(decoder_1_out12), .out13(decoder_1_out13), .out14(decoder_1_out14), .out15(decoder_1_out15),
    .out16(decoder_1_out16), .out17(decoder_1_out17), .out18(decoder_1_out18), .out19(decoder_1_out19),
    .out20(decoder_1_out20), .out21(decoder_1_out21), .out22(decoder_1_out22), .out23(decoder_1_out23),
    .out24(decoder_1_out24), .out25(decoder_1_out25), .out26(decoder_1_out26), .out27(decoder_1_out27),
    .out28(decoder_1_out28), .out29(decoder_1_out29), .out30(decoder_1_out30), .out31(decoder_1_out31),
    .sel(wreg));
  and and_1 (and_1_out, decoder_1_out1, clock_1_out);
  and and_2 (and_2_out, decoder_1_out2, clock_1_out, regwrite);
  and and_3 (and_3_out, decoder_1_out3, clock_1_out, regwrite);
  and and_4 (and_4_out, decoder_1_out4, clock_1_out, regwrite);
  and and_5 (and_5_out, decoder_1_out5, clock_1_out, regwrite);
  and and_6 (and_6_out, decoder_1_out6, clock_1_out, regwrite);
  and and_7 (and_7_out, decoder_1_out7, clock_1_out, regwrite);
  and and_8 (and_8_out, decoder_1_out8, clock_1_out, regwrite);
  and and_9 (and_9_out, decoder_1_out9, clock_1_out, regwrite);
  and and_10 (and_10_out, decoder_1_out10, clock_1_out, regwrite);
  and and_11 (and_11_out, decoder_1_out11, clock_1_out, regwrite);
  and and_12 (and_12_out, decoder_1_out12, clock_1_out, regwrite);
  and and_13 (and_13_out, decoder_1_out13, clock_1_out, regwrite);
  and and_14 (and_14_out, decoder_1_out14, clock_1_out, regwrite);
  and and_15 (and_15_out, decoder_1_out15, clock_1_out, regwrite);
  and and_16 (and_16_out, decoder_1_out16, clock_1_out, regwrite);
  and and_17 (and_17_out, decoder_1_out17, clock_1_out, regwrite);
  and and_18 (and_18_out, decoder_1_out18, clock_1_out, regwrite);
  and and_19 (and_19_out, decoder_1_out19, clock_1_out, regwrite);
  and and_20 (and_20_out, decoder_1_out20, clock_1_out, regwrite);
  and and_21 (and_21_out, decoder_1_out21, clock_1_out, regwrite);
  and and_22 (and_22_out, decoder_1_out22, clock_1_out, regwrite);
  and and_23 (and_23_out, decoder_1_out23, clock_1_out, regwrite);
  and and_24 (and_24_out, decoder_1_out24, clock_1_out, regwrite);
  and and_25 (and_25_out, decoder_1_out25, clock_1_out, regwrite);
  and and_26 (and_26_out, decoder_1_out26, clock_1_out, regwrite);
  and and_27 (and_27_out, decoder_1_out27, clock_1_out, regwrite);
  and and_28 (and_28_out, decoder_1_out28, clock_1_out, regwrite);
  and and_29 (and_29_out, decoder_1_out29, clock_1_out, regwrite);
  and and_30 (and_30_out, decoder_1_out30, clock_1_out, regwrite);
  and and_31 (and_31_out, decoder_1_out31, clock_1_out, regwrite);
  and and_32 (and_32_out, decoder_1_out0, clock_1_out, regwrite);
  Register #(.width(32)) reg0 (.D(wdata), .Q(reg0_q), .clk(and_32_out));  // open: en, clr
  Register #(.width(32)) u_reg2 (.D(wdata), .Q(reg2_q), .clk(and_2_out));  // open: en, clr
  Register #(.width(32)) reg4 (.D(wdata), .Q(reg4_q), .clk(and_4_out));  // open: en, clr
  Register #(.width(32)) reg6 (.D(wdata), .Q(reg6_q), .clk(and_6_out));  // open: en, clr
  Register #(.width(32)) reg8 (.D(wdata), .Q(reg8_q), .clk(and_8_out));  // open: en, clr
  Register #(.width(32)) reg10 (.D(wdata), .Q(reg10_q), .clk(and_10_out));  // open: en, clr
  Register #(.width(32)) reg12 (.D(wdata), .Q(reg12_q), .clk(and_12_out));  // open: en, clr
  Register #(.width(32)) reg14 (.D(wdata), .Q(reg14_q), .clk(and_14_out));  // open: en, clr
  Register #(.width(32)) reg16 (.D(wdata), .Q(reg16_q), .clk(and_16_out));  // open: en, clr
  Register #(.width(32)) reg18 (.D(wdata), .Q(reg18_q), .clk(and_18_out));  // open: en, clr
  Register #(.width(32)) reg20 (.D(wdata), .Q(reg20_q), .clk(and_20_out));  // open: en, clr
  Register #(.width(32)) reg22 (.D(wdata), .Q(reg22_q), .clk(and_22_out));  // open: en, clr
  Register #(.width(32)) reg24 (.D(wdata), .Q(reg24_q), .clk(and_24_out));  // open: en, clr
  Register #(.width(32)) reg26 (.D(wdata), .Q(reg26_q), .clk(and_26_out));  // open: en, clr
  Register #(.width(32)) reg28 (.D(wdata), .Q(reg28_q), .clk(and_28_out));  // open: en, clr
  Register #(.width(32)) reg30 (.D(wdata), .Q(reg30_q), .clk(and_30_out));  // open: en, clr
  Register #(.width(32)) u_reg1 (.D(wdata), .Q(reg1_q), .clk(and_1_out));  // open: en, clr
  Register #(.width(32)) reg3 (.D(wdata), .Q(reg3_q), .clk(and_3_out));  // open: en, clr
  Register #(.width(32)) reg5 (.D(wdata), .Q(reg5_q), .clk(and_5_out));  // open: en, clr
  Register #(.width(32)) reg7 (.D(wdata), .Q(reg7_q), .clk(and_7_out));  // open: en, clr
  Register #(.width(32)) reg9 (.D(wdata), .Q(reg9_q), .clk(and_9_out));  // open: en, clr
  Register #(.width(32)) reg11 (.D(wdata), .Q(reg11_q), .clk(and_11_out));  // open: en, clr
  Register #(.width(32)) reg13 (.D(wdata), .Q(reg13_q), .clk(and_13_out));  // open: en, clr
  Register #(.width(32)) reg15 (.D(wdata), .Q(reg15_q), .clk(and_15_out));  // open: en, clr
  Register #(.width(32)) reg17 (.D(wdata), .Q(reg17_q), .clk(and_17_out));  // open: en, clr
  Register #(.width(32)) reg19 (.D(wdata), .Q(reg19_q), .clk(and_19_out));  // open: en, clr
  Register #(.width(32)) reg21 (.D(wdata), .Q(reg21_q), .clk(and_21_out));  // open: en, clr
  Register #(.width(32)) reg23 (.D(wdata), .Q(reg23_q), .clk(and_23_out));  // open: en, clr
  Register #(.width(32)) reg25 (.D(wdata), .Q(reg25_q), .clk(and_25_out));  // open: en, clr
  Register #(.width(32)) reg27 (.D(wdata), .Q(reg27_q), .clk(and_27_out));  // open: en, clr
  Register #(.width(32)) reg29 (.D(wdata), .Q(reg29_q), .clk(and_29_out));  // open: en, clr
  Register #(.width(32)) reg31 (.D(wdata), .Q(reg31_q), .clk(and_31_out));  // open: en, clr
  Multiplexer #(.select(5), .width(32)) multiplexer_1 (
    .in0(reg0_q), .in1(reg1_q), .in2(reg2_q), .in3(reg3_q), .in4(reg4_q), .in5(reg5_q), .in6(reg6_q),
    .in7(reg7_q), .in8(reg8_q), .in9(reg9_q), .in10(reg10_q), .in11(reg11_q), .in12(reg12_q), .in13(reg13_q),
    .in14(reg14_q), .in15(reg15_q), .in16(reg16_q), .in17(reg17_q), .in18(reg18_q), .in19(reg19_q),
    .in20(reg20_q), .in21(reg21_q), .in22(reg22_q), .in23(reg23_q), .in24(reg24_q), .in25(reg25_q),
    .in26(reg26_q), .in27(reg27_q), .in28(reg28_q), .in29(reg29_q), .in30(reg30_q), .in31(reg31_q),
    .out(Rdata1), .sel(reg1));  // open: en
  Multiplexer #(.select(5), .width(32)) multiplexer_2 (
    .in0(reg0_q), .in1(reg1_q), .in2(reg2_q), .in3(reg3_q), .in4(reg4_q), .in5(reg5_q), .in6(reg6_q),
    .in7(reg7_q), .in8(reg8_q), .in9(reg9_q), .in10(reg10_q), .in11(reg11_q), .in12(reg12_q), .in13(reg13_q),
    .in14(reg14_q), .in15(reg15_q), .in16(reg16_q), .in17(reg17_q), .in18(reg18_q), .in19(reg19_q),
    .in20(reg20_q), .in21(reg21_q), .in22(reg22_q), .in23(reg23_q), .in24(reg24_q), .in25(reg25_q),
    .in26(reg26_q), .in27(reg27_q), .in28(reg28_q), .in29(reg29_q), .in30(reg30_q), .in31(reg31_q),
    .out(Rdata2), .sel(reg2));  // open: en
endmodule

module ALU (
  input  [31:0] A,
  input  [31:0] B,
  input  [3:0] ALUOperate,
  output [31:0] result,
  output Zero
);

  wire clock_1_out, comparator_1_eq, decoder_1_out0, decoder_1_out1, decoder_1_out3, decoder_1_out6,
       priority_encoder_1_gs;
  wire [1:0] priority_encoder_1_out;
  wire [31:0] adder_1_out, and_1_out, or_1_out, subtractor_1_out;

  Clock clock_1 (.out(clock_1_out));
  Decoder #(.select(4)) decoder_1 (
    .out0(decoder_1_out0), .out1(decoder_1_out1), .out3(decoder_1_out3), .out6(decoder_1_out6),
    .sel(ALUOperate));  // open: out2, out4, out5, out7, out8, out9, out10, out11, out12, out13, out14, out15, en
  assign and_1_out = A & B;  // AND_Gate and_1, 32 bits wide
  assign or_1_out = A | B;  // OR_Gate or_1, 32 bits wide
  Priority_Encoder #(.select(2)) priority_encoder_1 (
    .in0(decoder_1_out0), .in1(decoder_1_out1), .in2(decoder_1_out3), .in3(decoder_1_out6),
    .out(priority_encoder_1_out), .gs(priority_encoder_1_gs));  // open: en_out, en_in
  Adder #(.width(32)) adder_1 (.a(A), .b(B), .out(adder_1_out));  // open: cin, cout
  Subtractor #(.width(32)) subtractor_1 (.a(A), .b(B), .out(subtractor_1_out));  // open: bin, bout
  Comparator #(.width(32)) comparator_1 (.a(subtractor_1_out), .b({32{1'b0}}), .eq(comparator_1_eq));  // open: gt, lt
  Multiplexer #(.select(2), .width(32)) multiplexer_1 (
    .in0(and_1_out), .in1(or_1_out), .in2(adder_1_out), .in3(subtractor_1_out), .out(result),
    .sel(priority_encoder_1_out), .en(clock_1_out));
  Multiplexer multiplexer_2 (.in0(1'b0), .in1(comparator_1_eq), .out(Zero), .sel(clock_1_out));  // open: en
endmodule

module Control (
  input  [5:0] opcode,
  output regdst,
  output alusrc,
  output mem2reg,
  output regwrite,
  output memwrite,
  output memread,
  output nPC_Sel,
  output ExtOp,
  output [1:0] ALUOp
);

  wire not_1_out, not_2_out, not_3_out, not_4_out, not_5_out, not_6_out, not_7_out, not_8_out, not_9_out,
       not_10_out, not_11_out, not_12_out, not_13_out, not_14_out, not_15_out, not_16_out;

  not not_1 (not_1_out, opcode[5]);
  not not_2 (not_2_out, opcode[5]);
  not not_3 (not_3_out, opcode[5]);
  not not_4 (not_4_out, opcode[5]);
  and R_Format (ALUOp[1], not_3_out, not_1_out, not_2_out, not_4_out, not_6_out, not_7_out);
  not not_5 (not_5_out, opcode[5]);
  not not_6 (not_6_out, opcode[5]);
  not not_7 (not_7_out, opcode[5]);
  not not_8 (not_8_out, opcode[5]);
  not not_9 (not_9_out, opcode[5]);
  and LW (mem2reg, opcode[5], not_5_out, not_9_out, not_8_out, opcode[5], opcode[5]);
  not not_10 (not_10_out, opcode[5]);
  not not_11 (not_11_out, opcode[5]);
  and SW (memwrite, opcode[5], not_11_out, opcode[5], not_10_out, opcode[5], opcode[5]);
  not not_12 (not_12_out, opcode[5]);
  not not_13 (not_13_out, opcode[5]);
  not not_14 (not_14_out, opcode[5]);
  and Beq (ALUOp[0], not_14_out, not_13_out, not_12_out, opcode[5], not_16_out, not_15_out);
  not not_15 (not_15_out, opcode[5]);
  not not_16 (not_16_out, opcode[5]);
  or or_1 (alusrc, mem2reg, memwrite);
  or or_2 (regwrite, ALUOp[1], mem2reg);
  or or_3 (ExtOp, mem2reg, memwrite, ALUOp[0]);

  assign memread = mem2reg;
  assign nPC_Sel = ALUOp[0];
  assign opcode[4:0] = {5{opcode[5]}};
  assign regdst = ALUOp[1];
endmodule

module IFU (
  input  IfBeqZero,
  input  [31:0] PCBeq,
  input  Reset,
  output [31:0] instr
);

  wire clock_1_out;
  wire [4:0] priority_encoder_1_out;
  wire [29:0] adder_1_out, adder_2_out, bit_extender_1_out, PC, PC_q;
  wire [31:0] shifter_1_out;

  Clock clock_1 (.out(clock_1_out));
  Register #(.width(30)) u_PC (.D(PC), .Q(PC_q), .clk(clock_1_out), .clr(Reset));  // open: en
  Shifter #(.width(32)) shifter_1 (.in(PCBeq), .\dist (5'b00010), .out(shifter_1_out));
  Priority_Encoder #(.select(5)) priority_encoder_1 (
    .in0(PC_q[0]), .in1(PC_q[1]), .in2(PC_q[2]), .in3(PC_q[3]), .in4(PC_q[4]), .in5(PC_q[5]), .in6(PC_q[6]),
    .in7(PC_q[7]), .in8(PC_q[8]), .in9(PC_q[9]), .in10(PC_q[10]), .in11(PC_q[11]), .in12(PC_q[12]),
    .in13(PC_q[13]), .in14(PC_q[14]), .in15(PC_q[15]), .in16(PC_q[16]), .in17(PC_q[17]), .in18(PC_q[18]),
    .in19(PC_q[19]), .in20(PC_q[20]), .in21(PC_q[21]), .in22(PC_q[22]), .in23(PC_q[23]), .in24(PC_q[24]),
    .in25(PC_q[25]), .in26(PC_q[26]), .in27(PC_q[27]), .in28(PC_q[28]), .in29(PC_q[29]), .in30(1'b0),
    .in31(1'b0), .out(priority_encoder_1_out));  // open: gs, en_out, en_in
  Bit_Extender #(.in_width(32), .out_width(30)) bit_extender_1 (.in(shifter_1_out), .out(bit_extender_1_out));
  Adder #(.width(30)) adder_1 (.a(30'h4), .b(PC_q), .out(adder_1_out));  // open: cin, cout
  ROM #(.addrWidth(5), .dataWidth(32)) rom_1 (.addr(priority_encoder_1_out), .data(instr));  // open: sel
  Adder #(.width(30)) adder_2 (.a(bit_extender_1_out), .b(adder_1_out), .out(adder_2_out));  // open: cin, cout
  Multiplexer #(.width(30)) multiplexer_1 (
    .in0(adder_1_out), .in1(adder_2_out), .out(PC), .sel(IfBeqZero));  // open: en
endmodule

module Extender (
  input  [15:0] in_1,
  input  ExtOp,
  output [31:0] out_3
);

  wire [15:0] multiplexer_1_out;

  assign out_3 = {{16{1'b0}}, multiplexer_1_out};  // Bit_Extender bit_extender_1
  Multiplexer #(.width(16)) multiplexer_1 (
    .in0({16{1'b0}}), .in1(in_1), .out(multiplexer_1_out), .sel(ExtOp));  // open: en
endmodule

module ALUControl (
  input  [5:0] Funct,
  input  [1:0] in_2,
  output [3:0] ALUOperate
);

  wire decoder_1_out0, decoder_1_out1, decoder_1_out2, decoder_1_out3, decoder_2_out5, decoder_2_out6;

  Decoder #(.select(2), .enable("false")) decoder_1 (
    .out0(decoder_1_out0), .out1(decoder_1_out1), .out2(decoder_1_out2), .out3(decoder_1_out3), .sel(in_2));
  LED led_1 (.in(decoder_1_out3));
  Decoder #(.select(3)) decoder_2 (
    .out0(decoder_1_out0), .out4(decoder_1_out1), .out5(decoder_2_out5), .out6(decoder_2_out6),
    .sel(Funct[5:3]), .en(decoder_1_out2));  // open: out1, out2, out3, out7
  Priority_Encoder #(.select(4)) priority_encoder_1 (
    .in0(decoder_2_out6), .in1(decoder_2_out5), .in2(decoder_1_out0), .in6(decoder_1_out1), .out(ALUOperate));  // open: in3, in4, in5, in7, in8, in9, in10, in11, in12, in13, in14, in15, gs, en_out, en_in
endmodule
